# Fritzing sketch diagrama (saved by Fritzing 1.0.1rc)

parts:
  Componente1 = Arduino Nano (Rev3.0)
  Grove1 = Grove OLED 128x96
  RE1 = KY-040 Rotary encoder [package=THT]
  Pololu_A1 = Pololu A4988 [package=SO16]
  M1 = Stepper Motor - Bipolar  # not connected
  U1 = RELAY [package=relay-jzc]

nets:
  GND: Componente1.GND, Grove1.GND, RE1.GND, Pololu_A1.GND, U1.MAIN
  N1: Componente1.D2, Pololu_A1.STEP
  N2: Componente1.D3, Pololu_A1.DIR
  N3: Componente1.D4, RE1.CLK
  N4: Componente1.D5, RE1.DT
  N5: Componente1.D6, RE1.SW
  N6: Componente1.D7, U1.COIL1
  N7: Componente1.D8, Pololu_A1.ENABLE
  5V: Componente1.5V, RE1.Vcc
  N8: Componente1.A5, Grove1.SCL
  N9: Componente1.A4, Grove1.SDA

custom parts:
  KY-040 Rotary encoder: KY-040 Rotary Encoder with switch on breakout borad from AZ Delivery
